# Fritzing sketch Array (saved by Fritzing 0.9.3b)
breadboards: 6

parts:
  hc-sr1 = hc-sr04
  R1 = Resistor [tolerance=±5% resistance=220 package=THT]
  R2 = Resistor [tolerance=±5% resistance=2.2k package=THT]
  hc-sr2 = hc-sr04
  R3 = Resistor [tolerance=±5% resistance=220 package=THT]
  R4 = Resistor [tolerance=±5% resistance=2.2k package=THT]
  hc-sr3 = hc-sr04
  R5 = Resistor [tolerance=±5% resistance=220 package=THT]
  R6 = Resistor [tolerance=±5% resistance=2.2k package=THT]
  hc-sr4 = hc-sr04
  R7 = Resistor [tolerance=±5% resistance=220 package=THT]
  R8 = Resistor [tolerance=±5% resistance=2.2k package=THT]
  hc-sr5 = hc-sr04
  R9 = Resistor [tolerance=±5% resistance=220 package=THT]
  R10 = Resistor [tolerance=±5% resistance=2.2k package=THT]
  Raspberry_Pi_1 = Raspberry Pi 3 [part_number=RPI-3-V1.2]
  IC2 = IC, DIP package, 16 pins [chip_label=SN54HC595]
  R11 = Resistor [tolerance=±5% resistance=4.7k package=THT]
  R19 = Resistor [tolerance=±5% resistance=150 package=THT]
  R20 = Resistor [tolerance=±5% resistance=150 package=THT]
  R21 = Resistor [tolerance=±5% resistance=100 package=THT]
  LED7 = RGB LED (com. cathode, rgb) [package="5 mm [THT]"]

nets:
  VCC: hc-sr1.VCC, hc-sr2.VCC, hc-sr3.VCC, hc-sr4.VCC, hc-sr5.VCC, Raspberry_Pi_1.5V, IC2.pin16
  N1: hc-sr1.Trig, IC2.pin2
  N2: hc-sr1.Echo, R1.Pin_1
  GND: hc-sr1.GND, hc-sr2.GND, hc-sr3.GND, hc-sr4.GND, hc-sr5.GND, Raspberry_Pi_1.GND, IC2.pin8, IC2.pin13, R11.Pin_1, LED7.common_cathode
  N3: R1.Pin_0, R2.Pin_0
  N4: R2.Pin_1, R4.Pin_1, R6.Pin_1, R8.Pin_1, R10.Pin_1, Raspberry_Pi_1.GPIO23, R11.Pin_0
  N5: hc-sr2.Trig, IC2.pin4
  N6: hc-sr2.Echo, R3.Pin_1
  N7: R3.Pin_0, R4.Pin_0
  N8: hc-sr3.Trig, IC2.pin3
  N9: hc-sr3.Echo, R5.Pin_1
  N10: R5.Pin_0, R6.Pin_0
  N11: hc-sr4.Trig, IC2.pin15
  N12: hc-sr4.Echo, R7.Pin_1
  N13: R7.Pin_0, R8.Pin_0
  N14: hc-sr5.Trig, IC2.pin1
  N15: hc-sr5.Echo, R9.Pin_1
  N16: R9.Pin_0, R10.Pin_0
  N17: Raspberry_Pi_1.GPIO4, IC2.pin10
  N18: Raspberry_Pi_1.GPIO17, IC2.pin14
  N19: Raspberry_Pi_1.GPIO27, IC2.pin12
  N20: Raspberry_Pi_1.GPIO22, IC2.pin11
  N21: IC2.pin5, R21.Pin_0
  N22: IC2.pin6, R20.Pin_0
  N23: IC2.pin7, R19.Pin_0
  N24: R19.Pin_1, LED7.blue_anode
  N25: R20.Pin_1, LED7.green_anode
  N26: R21.Pin_1, LED7.red_anode
