# Fritzing sketch Lights (saved by Fritzing 0.9.3b)
breadboards: 2

parts:
  Raspberry_Pi_1 = Raspberry Pi 3 [part_number=RPI-3-V1.2]
  IC1 = IC, DIP package, 16 pins [chip_label=SN54HC595]
  IC2 = IC, DIP package, 16 pins [chip_label=SN54HC595]
  IC3 = IC, DIP package, 16 pins [chip_label=SN54HC595]
  R1 = Resistor [tolerance=±5% resistance=150 package=THT]
  R2 = Resistor [tolerance=±5% resistance=150 package=THT]
  R3 = Resistor [tolerance=±5% resistance=100 package=THT]
  LED1 = RGB LED (com. cathode, rgb) [package="5 mm [THT]"]
  LED2 = RGB LED (com. cathode, rgb) [package="5 mm [THT]"]
  LED3 = RGB LED (com. cathode, rgb) [package="5 mm [THT]"]
  LED4 = RGB LED (com. cathode, rgb) [package="5 mm [THT]"]
  LED5 = RGB LED (com. cathode, rgb) [package="5 mm [THT]"]
  LED6 = RGB LED (com. cathode, rgb) [package="5 mm [THT]"]
  LED7 = RGB LED (com. cathode, rgb) [package="5 mm [THT]"]
  VCC1 = Battery
  R4 = Resistor [tolerance=±5% resistance=150 package=THT]
  R5 = Resistor [tolerance=±5% resistance=150 package=THT]
  R6 = Resistor [tolerance=±5% resistance=100 package=THT]
  R7 = Resistor [tolerance=±5% resistance=150 package=THT]
  R8 = Resistor [tolerance=±5% resistance=150 package=THT]
  R9 = Resistor [tolerance=±5% resistance=100 package=THT]
  R10 = Resistor [tolerance=±5% resistance=150 package=THT]
  R11 = Resistor [tolerance=±5% resistance=150 package=THT]
  R12 = Resistor [tolerance=±5% resistance=100 package=THT]
  R13 = Resistor [tolerance=±5% resistance=150 package=THT]
  R14 = Resistor [tolerance=±5% resistance=150 package=THT]
  R15 = Resistor [tolerance=±5% resistance=100 package=THT]
  R16 = Resistor [tolerance=±5% resistance=150 package=THT]
  R17 = Resistor [tolerance=±5% resistance=150 package=THT]
  R18 = Resistor [tolerance=±5% resistance=100 package=THT]
  R19 = Resistor [tolerance=±5% resistance=150 package=THT]
  R20 = Resistor [tolerance=±5% resistance=150 package=THT]
  R21 = Resistor [tolerance=±5% resistance=100 package=THT]

nets:
  N1: Raspberry_Pi_1.GPIO6, IC1.pin11, IC2.pin11, IC3.pin11
  N2: Raspberry_Pi_1.GPIO13, IC2.pin12
  N3: Raspberry_Pi_1.GPIO19, IC3.pin12
  N4: Raspberry_Pi_1.GND, IC1.pin8, IC1.pin13, IC2.pin8, IC2.pin13, IC3.pin8, IC3.pin13, LED1.common_cathode, LED2.common_cathode, LED3.common_cathode, LED4.common_cathode, LED5.common_cathode, LED6.common_cathode, LED7.common_cathode, VCC1.-
  N5: Raspberry_Pi_1.GPIO16, IC1.pin12
  N6: Raspberry_Pi_1.GPIO12, IC1.pin14, IC2.pin14, IC3.pin14
  N7: IC1.pin1, R1.Pin_1
  N8: IC1.pin2, R4.Pin_1
  N9: IC1.pin3, R7.Pin_1
  N10: IC1.pin4, R10.Pin_1
  N11: IC1.pin5, R13.Pin_1
  N12: IC1.pin6, R16.Pin_1
  N13: IC1.pin7, R19.Pin_1
  N14: IC1.pin10, IC1.pin16, IC2.pin10, IC2.pin16, IC3.pin10, IC3.pin16, VCC1.+
  N15: IC2.pin1, R2.Pin_1
  N16: IC2.pin2, R5.Pin_1
  N17: IC2.pin3, R8.Pin_1
  N18: IC2.pin4, R11.Pin_1
  N19: IC2.pin5, R14.Pin_1
  N20: IC2.pin6, R17.Pin_1
  N21: IC2.pin7, R20.Pin_1
  N22: IC3.pin1, R3.Pin_1
  N23: IC3.pin2, R6.Pin_1
  N24: IC3.pin3, R9.Pin_1
  N25: IC3.pin4, R12.Pin_1
  N26: IC3.pin5, R15.Pin_1
  N27: IC3.pin6, R18.Pin_1
  N28: IC3.pin7, R21.Pin_1
  N29: R1.Pin_0, LED1.blue_anode
  N30: R2.Pin_0, LED1.green_anode
  N31: R3.Pin_0, LED1.red_anode
  N32: LED2.red_anode, R6.Pin_0
  N33: LED2.green_anode, R5.Pin_0
  N34: LED2.blue_anode, R4.Pin_0
  N35: LED3.red_anode, R9.Pin_0
  N36: LED3.green_anode, R8.Pin_0
  N37: LED3.blue_anode, R7.Pin_0
  N38: LED4.red_anode, R12.Pin_0
  N39: LED4.green_anode, R11.Pin_0
  N40: LED4.blue_anode, R10.Pin_0
  N41: LED5.red_anode, R15.Pin_0
  N42: LED5.green_anode, R14.Pin_0
  N43: LED5.blue_anode, R13.Pin_0
  N44: LED6.red_anode, R18.Pin_0
  N45: LED6.green_anode, R17.Pin_0
  N46: LED6.blue_anode, R16.Pin_0
  N47: LED7.red_anode, R21.Pin_0
  N48: LED7.green_anode, R20.Pin_0
  N49: LED7.blue_anode, R19.Pin_0

notes:
  Seperate Power Supply
  Each LED represents a row of 7
