# Fritzing sketch sliders (saved by Fritzing 0.9.3b)
breadboards: 3

parts:
  R1 = Slide Potentiometer [maximum_resistance=100kΩ]
  R2 = Slide Potentiometer [maximum_resistance=100kΩ]
  R3 = Slide Potentiometer [maximum_resistance=100kΩ]
  R4 = Slide Potentiometer [maximum_resistance=100kΩ]
  IC1 = IC, DIP package, 16 pins [chip_label=MCP3008]
  Raspberry_Pi_1 = Raspberry Pi 3 [part_number=RPI-3-V1.2]
  R5 = Slide Potentiometer [maximum_resistance=100kΩ]

nets:
  N1: R1.leg1, R2.leg1, R3.leg1, R4.leg1, IC1.pin15, IC1.pin16, Raspberry_Pi_1.5V, R5.leg1
  N2: R1.wiper, IC1.pin3
  N3: R1.leg2, R2.leg2, R3.leg2, R4.leg2, IC1.pin5, IC1.pin6, IC1.pin7, IC1.pin8, IC1.pin9, IC1.pin14, Raspberry_Pi_1.GND, R5.leg2
  N4: R2.wiper, IC1.pin4
  N5: R3.wiper, IC1.pin2
  N6: R4.wiper, IC1.pin1, R5.wiper
  N7: IC1.pin10, Raspberry_Pi_1.GPIO8
  N8: IC1.pin11, Raspberry_Pi_1.GPIO10
  N9: IC1.pin12, Raspberry_Pi_1.GPIO9
  N10: IC1.pin13, Raspberry_Pi_1.GPIO11
